# Fritzing sketch Slave_V2 (saved by Fritzing 0.9.3b)
stripboards: 1

parts:
  U2 = Header 8 [package=1x08_smd]
  U3 = Header 8 [package=1x08_smd]
  S3 = Pushbutton [package="[THT]"]
  R1 = Resistor [tolerance=±5% resistance=10k package="0603 [SMD]"]
  JP1 = Header 6 [package=1x06_smd_straight_alt]
  R2 = Resistor [tolerance=±5% resistance=220 package="0603 [SMD]"]
  JP3 = Header 6 [package=1x06_smd_straight_alt]
  J6 = female pin header, 4 pins [form="♀ (female)"]
  J7 = female pin header, 3 pins [form="♀ (female)"]
  J10 = female pin header, 5 pins [form="♀ (female)"]
  J9 = male pin header, 20 pins [form="♂ (male)"]
  J8 = male pin header, 20 pins [form="♂ (male)"]
  JP4 = Header 6 [package=1x06_smd_straight_alt]
  JP5 = Header 6 [package=1x06_smd_straight_alt]
  J11 = female pin header, 4 pins [form="♀ (female)"]
  J12 = female pin header, 3 pins [form="♀ (female)"]
  J13 = female pin header, 2 pins [form="♀ (female)"]
  R3 = Resistor [tolerance=±5% resistance=220 package="0603 [SMD]"]

nets:
  N1: U2.1, JP1.1, JP3.1, J6.pin1, J10.pin5, J9.pin1, JP4.1, JP5.1, J11.pin1, R3.Pin_0
  N2: U2.2, R1.Pin_1, JP1.2, JP1.3, JP3.2, JP3.3, J6.pin2, J7.pin2, J10.pin1, J9.pin3, JP4.2, JP4.3, JP5.2, JP5.3, J11.pin2, J12.pin2
  N3: U2.3, JP1.4, JP4.4
  N4: U2.5, J9.pin4
  N5: U2.7, JP1.5, JP4.5
  N6: U2.8, R2.Pin_0
  N7: U3.1, S3.Pin_1, S3.Pin_2, J8.pin1, J13.pin2
  N8: U3.2, JP1.6, JP4.6
  N9: U3.3, S3.Pin_3, S3.Pin_4, R1.Pin_0, J13.pin1
  N10: R2.Pin_1, J7.pin3, J12.pin3
  N11: JP3.4, J8.pin18, JP5.4
  N12: JP3.5, J9.pin20, JP5.5
  N13: JP3.6, J9.pin6, JP5.6
  N14: J6.pin3, J8.pin2, J11.pin3
  N15: J6.pin4, J8.pin3, J11.pin4
  N16: J7.pin1, J12.pin1, R3.Pin_1

notes:
  Audio1
  Audio2
  I2C
  Ser
  MIDI
  Vert = 5, Jaune =2, Orange=4
  #2 VCC
  #3-SDA
  #5-SCL
  #6-Gnd
  #8-UART TX
  #12-I2S-BCK
  #40-I2S-DATA
  #35-I2S_LRCK
  #1 +3.3V
  USB
